// Logisim project lab1.5.circ as structural Verilog: 2 circuits, main circuit 4-1MUX
module _4_1MUX (
  input  D0,
  input  D1,
  input  D2,
  input  D3,
  input  S0,
  input  S1,
  output Y
);

  wire n2_1mux_1_y, n2_1mux_2_y;

  _2_1MUX u_2_1mux_1 (.D0(D0), .D1(D1), .S(S0), .Y(n2_1mux_1_y));
  _2_1MUX u_2_1mux_2 (.D0(D2), .D1(D3), .S(S0), .Y(n2_1mux_2_y));
  _2_1MUX u_2_1mux_3 (.D0(n2_1mux_1_y), .D1(n2_1mux_2_y), .S(S1), .Y(Y));

  // Notes on the sheet:
  //   输入引脚
  //   请勿修改引脚名称、电路名称及电路封装外观
  //   提示：使用二选一多路选择器子电路级联实现四选一多路选择器，禁止直接使用多路选择器组件。
  //   输出引脚
endmodule

module _2_1MUX (
  input  D0,
  input  D1,
  input  S,
  output Y
);

  wire transistor_1_out;

  Transistor transistor_1 (.in(1'b1), .out(transistor_1_out), .gate(S));
  Transistor #(.\type ("n")) transistor_2 (.in(1'b0), .out(transistor_1_out), .gate(S));
  // Transmission_Gate transmission_1: pin names not known; wires that end beside it: D0, S, transistor_1_out, Y
  // Transmission_Gate transmission_2: pin names not known; wires that end beside it: transistor_1_out, 1'b0, D1, transistor_1_out, S, Y

  // Notes on the sheet:
  //   输入引脚
  //   请勿修改引脚名称及电路封装外观
  //   提示：使用传输门和晶体管来实现二选一多路选择器，禁止直接使用选择器组件。
  //   输出引脚
endmodule
