// Logisim project lab4.3.circ as structural Verilog: 1 circuit, main circuit Adder32
// 加法器
module Adder32 (
  input  Cin,
  input  [31:0] X,
  input  [31:0] Y,
  output CF,
  output Cout,
  output OF,
  output SF,
  output [31:0] S,
  output ZF
);

  wire adder16_2_gg, adder16_2_pg, and_1_out, and_2_out, and_3_out, or_1_out;

  Adder16 adder16_1 (.X(X[31:16]), .Y(Y[31:16]), .C0(or_1_out), .S(S[31:16]), .C16(Cout));  // open: Pg, Gg
  or or_1 (or_1_out, adder16_2_gg, and_1_out);
  and and_1 (and_1_out, adder16_2_pg, Cin);
  and and_2 (and_2_out, S[31], ~X[31], ~Y[31]);  // AND_Gate
  and and_3 (and_3_out, ~S[31], X[31], Y[31]);  // AND_Gate
  or or_2 (OF, and_2_out, and_3_out);
  // Probe on X
  // Probe on Y
  // Probe on S
  Adder16 adder16_2 (
    .X(X[15:0]), .Y(Y[15:0]), .C0(Cin), .S(S[15:0]), .Pg(adder16_2_pg), .Gg(adder16_2_gg));  // open: C16
  Comparator #(.width(32)) comparator_1 (.a({32{1'b0}}), .b(S), .eq(ZF));  // open: gt, lt
  xor xor_1 (CF, Cin, Cout);

  assign SF = S[31];

  // Notes on the sheet:
  //   Y: pull=down
  //   X: pull=down
  //   Cin: pull=down
  //   输入引脚区
  //   输出引脚区
  //   请勿修改引脚名称、电路名称及电路封装外观
  //   提示：使用16位并行加法器子电路实现32位快速加法器
  //   功能说明:32位Adder  S=X+Y，Cout为最高位进位位，Cin为进位输入， S为和，溢出OF、进位CF、零ZF、符号SF。
  //   +
  //   =
  //   无符号加法
endmodule
